// Logisim project projet.circ as structural Verilog: 12 circuits, main circuit add1bit
module add1bit (
  input  a,
  input  b,
  input  c_in,
  output c_out,
  output s
);

  wire a_and_b_out, a_and_c_in_out, b_and_c_in_out, xor_1_a_xor_b;

  and a_and_b (a_and_b_out, a, b);
  and a_and_c_in (a_and_c_in_out, a, c_in);
  and b_and_c_in (b_and_c_in_out, b, c_in);
  \xor  xor_1 (.a(a), .b(b), .a_xor_b(xor_1_a_xor_b));
  or or_1 (c_out, a_and_b_out, a_and_c_in_out, b_and_c_in_out);
  \xor  xor_2 (.a(xor_1_a_xor_b), .b(c_in), .a_xor_b(s));
endmodule

module \xor  (
  input  a,
  input  b,
  output a_xor_b
);

  wire and_1_out, and_2_out, not_1_out, not_2_out;

  not not_1 (not_1_out, a);
  not not_2 (not_2_out, b);
  and and_1 (and_1_out, not_1_out, b);
  and and_2 (and_2_out, a, not_2_out);
  or or_1 (a_xor_b, and_1_out, and_2_out);
endmodule

module add8bits (
  input  [7:0] a,
  input  [7:0] b,
  input  c_in,
  output c_out,
  output [7:0] s
);

  wire add1bit_1_c_out, add1bit_2_c_out, add1bit_3_c_out, add1bit_4_c_out, add1bit_5_c_out, add1bit_6_c_out,
       add1bit_7_c_out;

  add1bit add1bit_1 (.a(a[0]), .b(b[0]), .c_in(c_in), .c_out(add1bit_1_c_out), .s(s[0]));
  add1bit add1bit_2 (.a(a[2]), .b(b[2]), .c_in(add1bit_3_c_out), .c_out(add1bit_2_c_out), .s(s[2]));
  add1bit add1bit_3 (.a(a[1]), .b(b[1]), .c_in(add1bit_1_c_out), .c_out(add1bit_3_c_out), .s(s[1]));
  add1bit add1bit_4 (.a(a[4]), .b(b[4]), .c_in(add1bit_5_c_out), .c_out(add1bit_4_c_out), .s(s[4]));
  add1bit add1bit_5 (.a(a[3]), .b(b[3]), .c_in(add1bit_2_c_out), .c_out(add1bit_5_c_out), .s(s[3]));
  add1bit add1bit_6 (.a(a[6]), .b(b[6]), .c_in(add1bit_7_c_out), .c_out(add1bit_6_c_out), .s(s[6]));
  add1bit add1bit_7 (.a(a[5]), .b(b[5]), .c_in(add1bit_4_c_out), .c_out(add1bit_7_c_out), .s(s[5]));
  add1bit add1bit_8 (.a(a[7]), .b(b[7]), .c_in(add1bit_6_c_out), .c_out(c_out), .s(s[7]));
endmodule

module add_sub_8bits (
  input  [7:0] a,
  input  [7:0] b,
  input  c_in,
  output c_out,
  output [7:0] s
);

  wire [7:0] cond_xor_1_b_out;

  cond_xor cond_xor_1 (.b_in(b), .c(c_in), .b_out(cond_xor_1_b_out));
  add8bits add8bits_1 (.a(a), .b(cond_xor_1_b_out), .c_in(c_in), .c_out(c_out), .s(s));
endmodule

module cond_xor (
  input  [7:0] b_in,
  input  c,
  output [7:0] b_out
);

  xor xor_1 (b_out[7], b_in[7], c);
  xor xor_2 (b_out[6], b_in[6], c);
  xor xor_3 (b_out[5], b_in[5], c);
  xor xor_4 (b_out[4], b_in[4], c);
  xor xor_5 (b_out[3], b_in[3], c);
  xor xor_6 (b_out[2], b_in[2], c);
  xor xor_7 (b_out[1], b_in[1], c);
  xor xor_8 (b_out[0], b_in[0], c);
endmodule

module latch (
  input  d,
  input  keep,
  output q
);

  Multiplexer #(.enable("false")) multiplexer_1 (.in0(q), .in1(d), .out(q), .sel(keep));
endmodule

module flip_flop (
  input  e,
  input  clk,
  output s
);

  wire latch_1_q, not_1_out;

  latch latch_1 (.d(e), .keep(clk), .q(latch_1_q));
  latch latch_2 (.d(latch_1_q), .keep(not_1_out), .q(s));
  not not_1 (not_1_out, clk);
endmodule

module flip_flop_reset (
  input  e,
  input  reset,
  input  clk,
  output s
);

  wire and_1_out, not_1_out;

  and and_1 (and_1_out, e, not_1_out);
  not not_1 (not_1_out, reset);
  flip_flop flip_flop_1 (.e(and_1_out), .clk(clk), .s(s));
endmodule

module register_1 (
  input  e,
  input  reset,
  input  enable,
  input  clk,
  output s
);

  wire and_1_out;

  flip_flop_reset flip_flop_reset_1 (.e(e), .reset(reset), .clk(and_1_out), .s(s));
  and and_1 (and_1_out, enable, clk);
endmodule

module register_8 (
  input  [7:0] e,
  input  reset,
  input  enable,
  input  clk,
  output [7:0] s
);

  register_1 register_1_1 (.e(e[2]), .reset(reset), .enable(enable), .clk(clk), .s(s[2]));
  register_1 register_1_2 (.e(e[1]), .reset(reset), .enable(enable), .clk(clk), .s(s[1]));
  register_1 register_1_3 (.e(e[0]), .reset(reset), .enable(enable), .clk(clk), .s(s[0]));
  register_1 register_1_4 (.e(e[4]), .reset(reset), .enable(enable), .clk(clk), .s(s[4]));
  register_1 register_1_5 (.e(e[3]), .reset(reset), .enable(enable), .clk(clk), .s(s[3]));
  register_1 register_1_6 (.e(e[7]), .reset(reset), .enable(enable), .clk(clk), .s(s[7]));
  register_1 register_1_7 (.e(e[6]), .reset(reset), .enable(enable), .clk(clk), .s(s[6]));
  register_1 register_1_8 (.e(e[5]), .reset(reset), .enable(enable), .clk(clk), .s(s[5]));
endmodule

module demux_1_to_8 (
  input  e,
  input  [2:0] select,
  output s0,
  output s1,
  output s2,
  output s3,
  output s4,
  output s5,
  output s6,
  output s7
);

  wire not_1_out, not_2_out, not_3_out, not_4_out, not_5_out, not_6_out, not_7_out, not_8_out, not_9_out,
       not_10_out, not_11_out, not_12_out;

  not not_1 (not_1_out, select[2]);
  not not_2 (not_2_out, select[1]);
  not not_3 (not_3_out, select[0]);
  not not_4 (not_4_out, select[2]);
  not not_5 (not_5_out, select[1]);
  not not_6 (not_6_out, select[2]);
  not not_7 (not_7_out, select[0]);
  not not_8 (not_8_out, select[2]);
  not not_9 (not_9_out, select[1]);
  not not_10 (not_10_out, select[0]);
  not not_11 (not_11_out, select[1]);
  not not_12 (not_12_out, select[0]);
  and and_1 (s0, e, not_1_out, not_2_out, not_3_out);
  and and_2 (s1, e, not_4_out, not_5_out, select[0]);
  and and_3 (s2, e, not_6_out, select[1], not_7_out);
  and and_4 (s3, e, not_8_out, select[1], select[0]);
  and and_5 (s4, e, select[2], not_9_out, not_10_out);
  and and_6 (s5, select[2], not_11_out, select[0]);
  and and_7 (s6, e, select[2], select[1], not_12_out);
  and and_8 (s7, e, select[2], select[1], select[0]);
endmodule

module mux_1_to_8 (
  input  e0,
  input  e1,
  input  e2,
  input  e3,
  input  e4,
  input  e5,
  input  e6,
  input  e7,
  input  [2:0] select,
  output s
);

  wire and_1_out, and_2_out, and_3_out, and_4_out, and_5_out, and_6_out, and_7_out, and_8_out, not_1_out,
       not_2_out, not_3_out, not_4_out, not_5_out, not_6_out, not_7_out, not_8_out, not_9_out, not_10_out,
       not_11_out, not_12_out;

  not not_1 (not_1_out, select[2]);
  and and_1 (and_1_out, e0, not_1_out, not_2_out, not_3_out);
  not not_2 (not_2_out, select[1]);
  not not_3 (not_3_out, select[0]);
  not not_4 (not_4_out, select[2]);
  and and_2 (and_2_out, e1, not_4_out, not_5_out, select[0]);
  not not_5 (not_5_out, select[1]);
  not not_6 (not_6_out, select[2]);
  and and_3 (and_3_out, e2, not_6_out, select[1], not_7_out);
  not not_7 (not_7_out, select[0]);
  not not_8 (not_8_out, select[2]);
  and and_4 (and_4_out, e3, not_8_out, select[1], select[0]);
  and and_5 (and_5_out, e4, select[2], not_9_out, not_10_out);
  not not_9 (not_9_out, select[1]);
  not not_10 (not_10_out, select[0]);
  and and_6 (and_6_out, e5, select[2], not_11_out, select[0]);
  not not_11 (not_11_out, select[1]);
  and and_7 (and_7_out, e6, select[2], select[1], not_12_out);
  not not_12 (not_12_out, select[0]);
  and and_8 (and_8_out, e7, select[2], select[1], select[0]);
  or or_1 (s, and_1_out, and_2_out, and_3_out, and_4_out, and_5_out, and_6_out, and_7_out, and_8_out);
endmodule
