// Logisim project tp2-diviseur.circ as structural Verilog: 6 circuits, main circuit automate
module q_2 (
  input  q0,
  input  q1,
  input  go,
  input  pp,
  output q_prime_2
);

  wire and_1_out, and_2_out, and_3_out, and_4_out, and_5_out, and_6_out, not_1_out, not_2_out, not_3_out,
       not_4_out, not_5_out, not_6_out, not_7_out, not_8_out, not_9_out, not_10_out, not_11_out;

  not not_1 (not_1_out, q0);
  not not_2 (not_2_out, q1);
  not not_3 (not_3_out, pp);
  not not_4 (not_4_out, q0);
  not not_5 (not_5_out, q1);
  not not_6 (not_6_out, q0);
  not not_7 (not_7_out, go);
  not not_8 (not_8_out, pp);
  not not_9 (not_9_out, q0);
  not not_10 (not_10_out, go);
  not not_11 (not_11_out, go);
  and and_1 (and_1_out, not_1_out, not_2_out, go, not_3_out);
  and and_2 (and_2_out, not_4_out, not_5_out, go, pp);
  and and_3 (and_3_out, not_6_out, q1, not_7_out, not_8_out);
  and and_4 (and_4_out, not_9_out, q1, not_10_out, pp);
  and and_5 (and_5_out, q0, q1, not_11_out, pp);
  and and_6 (and_6_out, q0, q1, go, pp);
  or or_1 (q_prime_2, and_1_out, and_2_out, and_3_out, and_4_out, and_5_out, and_6_out);
endmodule

module q_3 (
  input  q0,
  input  q1,
  input  go,
  input  pp,
  output q3
);

  wire and_1_out, and_2_out, and_3_out, and_4_out, and_5_out, and_6_out, and_7_out, and_8_out, not_1_out,
       not_2_out, not_3_out, not_4_out, not_5_out, not_6_out, not_7_out, not_8_out, not_9_out, not_10_out,
       not_11_out, not_12_out;

  not not_1 (not_1_out, q0);
  not not_2 (not_2_out, q1);
  not not_3 (not_3_out, pp);
  not not_4 (not_4_out, q0);
  not not_5 (not_5_out, q1);
  not not_6 (not_6_out, q0);
  not not_7 (not_7_out, pp);
  not not_8 (not_8_out, q0);
  not not_9 (not_9_out, go);
  not not_10 (not_10_out, pp);
  not not_11 (not_11_out, go);
  not not_12 (not_12_out, pp);
  and and_1 (and_1_out, not_1_out, not_2_out, go, not_3_out);
  and and_2 (and_2_out, not_4_out, not_5_out, go, pp);
  and and_3 (and_3_out, not_6_out, q1, go, not_7_out);
  and and_4 (and_4_out, not_8_out, q1, go, pp);
  and and_5 (and_5_out, q0, q1, not_9_out, not_10_out);
  and and_6 (and_6_out, q0, q1, not_11_out, pp);
  and and_7 (and_7_out, q0, q1, go, not_12_out);
  and and_8 (and_8_out, q0, q1, go, pp);
  or or_1 (q3, and_1_out, and_2_out, and_3_out, and_4_out, and_5_out, and_6_out, and_7_out, and_8_out);
endmodule

module sorties (
  input  q0,
  input  q1,
  output LoadN,
  output LoadP,
  output LoadX,
  output ResetX,
  output LoadQ,
  output ResetQ,
  output OK
);

  wire not_1_out, not_2_out, not_3_out;

  not not_1 (not_1_out, q0);
  not not_2 (not_2_out, q1);
  not not_3 (not_3_out, q0);
  and nq0_nq1 (LoadN, not_1_out, not_2_out);
  and q0_q1 (LoadQ, q0, q1);
  and nq0_q1 (OK, not_3_out, q1);

  assign LoadP = LoadN;
  assign LoadX = LoadQ;
  assign ResetQ = LoadN;
  assign ResetX = LoadN;
endmodule

module controle (
  input  go,
  input  pp,
  input  ck,
  input  reset,
  output LoadN,
  output LoadP,
  output LoadX,
  output ResetX,
  output LoadQ,
  output ResetQ,
  output OK
);

  wire q_2_1_q_prime_2, q_3_1_q3, register_1_q, register_2_q;

  q_2 q_2_1 (.q0(register_1_q), .q1(register_2_q), .go(go), .pp(pp), .q_prime_2(q_2_1_q_prime_2));
  q_3 q_3_1 (.q0(register_1_q), .q1(register_2_q), .go(go), .pp(pp), .q3(q_3_1_q3));
  Register #(.width(1)) register_1 (.D(q_2_1_q_prime_2), .en(1'b1), .Q(register_1_q), .clk(ck), .clr(reset));
  Register #(.width(1)) register_2 (.D(q_3_1_q3), .en(1'b1), .Q(register_2_q), .clk(ck), .clr(reset));
  sorties sorties_1 (
    .q0(register_1_q), .q1(register_2_q), .LoadN(LoadN), .LoadP(LoadP), .LoadX(LoadX), .ResetX(ResetX),
    .LoadQ(LoadQ), .ResetQ(ResetQ), .OK(OK));
endmodule

module comparateur (
  input  [7:0] A,
  input  [7:0] B,
  output S
);

  wire comparator_1_eq, comparator_1_gt, comparator_1_lt, not_1_out, or_1_out;

  Comparator comparator_1 (.a(A), .b(B), .gt(comparator_1_gt), .eq(comparator_1_eq), .lt(comparator_1_lt));
  or or_1 (or_1_out, comparator_1_eq, comparator_1_lt);
  not not_1 (not_1_out, comparator_1_gt);
  and and_1 (S, not_1_out, or_1_out);
endmodule

module automate (
  input  reset,
  input  go,
  input  [7:0] N,
  input  [7:0] P,
  output OK,
  output [7:0] Q
);

  wire clock_1_out, comparateur_1_s, controle_1_loadn, controle_1_loadp, controle_1_loadq, controle_1_loadx,
       controle_1_resetq, controle_1_resetx;
  wire [7:0] adder_1_out, adder_2_out, register_1_q, register_2_q, register_3_q, register_4_q;

  Clock clock_1 (.out(clock_1_out));
  Register register_1 (.D(N), .en(controle_1_loadn), .Q(register_1_q), .clk(clock_1_out));  // open: clr
  Register register_2 (
    .D(adder_1_out), .en(controle_1_loadx), .Q(register_2_q), .clk(clock_1_out), .clr(controle_1_resetx));
  Register register_3 (.D(P), .en(controle_1_loadp), .Q(register_3_q), .clk(clock_1_out));  // open: clr
  Register register_4 (
    .D(adder_2_out), .en(controle_1_loadq), .Q(register_4_q), .clk(clock_1_out), .clr(controle_1_resetq));
  controle controle_1 (
    .go(go), .pp(comparateur_1_s), .ck(clock_1_out), .reset(reset), .LoadN(controle_1_loadn),
    .LoadP(controle_1_loadp), .LoadX(controle_1_loadx), .ResetX(controle_1_resetx), .LoadQ(controle_1_loadq),
    .ResetQ(controle_1_resetq), .OK(OK));
  Adder adder_1 (.a(register_2_q), .b(register_3_q), .out(adder_1_out));  // open: cin, cout
  comparateur comparateur_1 (.B(register_1_q), .A(adder_1_out), .S(comparateur_1_s));
  Adder adder_2 (.a(register_4_q), .b(8'h1), .out(adder_2_out));  // open: cin, cout
  Subtractor subtractor_1 (.a(register_4_q), .b(8'h1), .out(Q));  // open: bin, bout
endmodule
