// Logisim project projet.circ as structural Verilog: 5 circuits, main circuit add1bit
module add1bit (
  input  a,
  input  b,
  input  c_in,
  output c_out,
  output s
);

  wire a_and_b_out, a_and_c_in_out, b_and_c_in_out, xor_1_a_xor_b;

  and a_and_b (a_and_b_out, a, b);
  and a_and_c_in (a_and_c_in_out, a, c_in);
  and b_and_c_in (b_and_c_in_out, b, c_in);
  \xor  xor_1 (.a(a), .b(b), .a_xor_b(xor_1_a_xor_b));
  or or_1 (c_out, a_and_b_out, a_and_c_in_out, b_and_c_in_out);
  \xor  xor_2 (.a(xor_1_a_xor_b), .b(c_in), .a_xor_b(s));
endmodule

module \xor  (
  input  a,
  input  b,
  output a_xor_b
);

  wire and_1_out, and_2_out, not_1_out, not_2_out;

  not not_1 (not_1_out, a);
  not not_2 (not_2_out, b);
  and and_1 (and_1_out, not_1_out, b);
  and and_2 (and_2_out, a, not_2_out);
  or or_1 (a_xor_b, and_1_out, and_2_out);
endmodule

module add8bits (
  input  [7:0] a,
  input  [7:0] b,
  input  c_in,
  output c_out,
  output [7:0] s
);

  wire add1bit_1_c_out, add1bit_2_c_out, add1bit_3_c_out, add1bit_4_c_out, add1bit_5_c_out, add1bit_6_c_out,
       add1bit_7_c_out;

  add1bit add1bit_1 (.a(a[0]), .b(b[0]), .c_in(c_in), .c_out(add1bit_1_c_out), .s(s[0]));
  add1bit add1bit_2 (.a(a[2]), .b(b[2]), .c_in(add1bit_3_c_out), .c_out(add1bit_2_c_out), .s(s[2]));
  add1bit add1bit_3 (.a(a[1]), .b(b[1]), .c_in(add1bit_1_c_out), .c_out(add1bit_3_c_out), .s(s[1]));
  add1bit add1bit_4 (.a(a[4]), .b(b[4]), .c_in(add1bit_5_c_out), .c_out(add1bit_4_c_out), .s(s[4]));
  add1bit add1bit_5 (.a(a[3]), .b(b[3]), .c_in(add1bit_2_c_out), .c_out(add1bit_5_c_out), .s(s[3]));
  add1bit add1bit_6 (.a(a[6]), .b(b[6]), .c_in(add1bit_7_c_out), .c_out(add1bit_6_c_out), .s(s[6]));
  add1bit add1bit_7 (.a(a[5]), .b(b[5]), .c_in(add1bit_4_c_out), .c_out(add1bit_7_c_out), .s(s[5]));
  add1bit add1bit_8 (.a(a[7]), .b(b[7]), .c_in(add1bit_6_c_out), .c_out(c_out), .s(s[7]));
endmodule

module add_sub_8bits (
  input  [7:0] a,
  input  [7:0] b,
  input  c_in,
  output c_out,
  output [7:0] s
);

  wire [7:0] cond_xor_1_b_out;

  cond_xor cond_xor_1 (.b_in(b), .c(c_in), .b_out(cond_xor_1_b_out));
  add8bits add8bits_1 (.a(a), .b(cond_xor_1_b_out), .c_in(c_in), .c_out(c_out), .s(s));
endmodule

module cond_xor (
  input  [7:0] b_in,
  input  c,
  output [7:0] b_out
);

  xor xor_1 (b_out[7], b_in[7], c);
  xor xor_2 (b_out[6], b_in[6], c);
  xor xor_3 (b_out[5], b_in[5], c);
  xor xor_4 (b_out[4], b_in[4], c);
  xor xor_5 (b_out[3], b_in[3], c);
  xor xor_6 (b_out[2], b_in[2], c);
  xor xor_7 (b_out[1], b_in[1], c);
  xor xor_8 (b_out[0], b_in[0], c);
endmodule
